// Logisim project ULA.circ as structural Verilog
module meiosomador (
  input  in_1,
  input  in_2,
  output out_3,
  output out_4
);

  xor Soma (out_3, in_1, in_2);
  and Carry_In (out_4, in_1, in_2);
endmodule

module somadorcompleto (
  input  Cin,
  input  A,
  input  B,
  output \Saída_Soma ,
  output Cout
);

  wire A___B_out, A___Cin_out, B__Cin_out, Soma_out;

  xor Soma (Soma_out, A, B);
  and A___B (A___B_out, A, B);
  and A___Cin (A___Cin_out, A, Cin);
  and B__Cin (B__Cin_out, B, Cin);
  xor plus_Cin (\Saída_Soma , Cin, Soma_out);
  or Out (Cout, A___B_out, A___Cin_out, B__Cin_out);
endmodule

module MUX32 (
  input  E0,
  input  E1,
  input  E2,
  input  E3,
  input  E4,
  input  E5,
  input  E6,
  input  E7,
  input  E8,
  input  E9,
  input  E10,
  input  E11,
  input  E12,
  input  E13,
  input  E14,
  input  E15,
  input  E16,
  input  E17,
  input  E18,
  input  E19,
  input  E20,
  input  E21,
  input  E22,
  input  E23,
  input  E24,
  input  E25,
  input  E26,
  input  E27,
  input  E28,
  input  E29,
  input  E30,
  input  E31,
  input  [4:0] in_33,
  output out_34
);

  wire mux16_1_out_21, mux16_2_out_21;

  MUX16 mux16_1 (
    .E0(E0), .E1(E1), .E2(E2), .E3(E3), .in_5(E4), .E5(E5), .E6(E6), .E7(E7), .E8(E8), .E9(E9), .E10(E10),
    .E11(E11), .in_13(E12), .E13(E13), .E14(E14), .E15(E15), .C(in_33[3]), .D(in_33[2]), .A(in_33[1]),
    .B(in_33[0]), .out_21(mux16_1_out_21));
  MUX16 mux16_2 (
    .E0(E16), .E1(E17), .E2(E18), .E3(E19), .in_5(E20), .E5(E21), .E6(E22), .E7(E23), .E8(E24), .E9(E25),
    .E10(E26), .E11(E27), .in_13(E28), .E13(E29), .E14(E30), .E15(E31), .C(in_33[3]), .D(in_33[2]),
    .A(in_33[1]), .B(in_33[0]), .out_21(mux16_2_out_21));
  MUX2 mux2_1 (.E0(mux16_1_out_21), .E1(mux16_2_out_21), .E(in_33[4]), .out_4(out_34));
endmodule

module MUX4 (
  input  in_1,
  input  in_2,
  input  in_3,
  input  in_4,
  input  in_5,
  input  in_6,
  output out_7
);

  wire and_1_out, and_2_out, and_3_out, and_4_out;

  and and_1 (and_1_out, in_1, ~in_5, ~in_6);  // AND_Gate
  and and_2 (and_2_out, in_2, ~in_5, in_6);  // AND_Gate
  and and_3 (and_3_out, in_3, in_5, ~in_6);  // AND_Gate
  and and_4 (and_4_out, in_4, in_5, in_6);
  or or_1 (out_7, and_1_out, and_2_out, and_3_out, and_4_out);
endmodule

module MUX16 (
  input  E0,
  input  E1,
  input  E2,
  input  E3,
  input  in_5,
  input  E5,
  input  E6,
  input  E7,
  input  E8,
  input  E9,
  input  E10,
  input  E11,
  input  in_13,
  input  E13,
  input  E14,
  input  E15,
  input  C,
  input  D,
  input  A,
  input  B,
  output out_21
);

  wire mux8_1_out_12, mux8_2_out_12;

  MUX8 mux8_1 (
    .E0(E0), .E1(E1), .E2(E2), .E3(E3), .E4(in_5), .E5(E5), .E6(E6), .E7(E7), .B(D), .C(A), .A(B),
    .out_12(mux8_1_out_12));
  MUX8 mux8_2 (
    .E0(E8), .E1(E9), .E2(E10), .E3(E11), .E4(in_13), .E5(E13), .E6(E14), .E7(E15), .B(D), .C(A), .A(B),
    .out_12(mux8_2_out_12));
  MUX2 mux2_1 (.E0(mux8_1_out_12), .E1(mux8_2_out_12), .E(C), .out_4(out_21));
endmodule

module MUX2 (
  input  E0,
  input  E1,
  input  E,
  output out_4
);

  wire and_1_out, and_2_out;

  and and_1 (and_1_out, E0, ~E);  // AND_Gate
  and and_2 (and_2_out, E1, E);
  or or_1 (out_4, and_1_out, and_2_out);
endmodule

module \CélulaULA  (
  input  A,
  input  B,
  input  Cin,
  input  [4:0] in_4,
  output Cout,
  output out_6
);

  wire and_1_out, or_1_out, \somadorcompleto_1_saída_soma , xor_1_out;

  and and_1 (and_1_out, A, B);
  or or_1 (or_1_out, A, B);
  xor xor_1 (xor_1_out, A, B);
  somadorcompleto somadorcompleto_1 (
    .Cin(Cin), .A(A), .B(B), .\Saída_Soma (\somadorcompleto_1_saída_soma ), .Cout(Cout));
  MUX32 mux32_1 (
    .E0(and_1_out), .E1(or_1_out), .E2(\somadorcompleto_1_saída_soma ), .E3(xor_1_out), .E4(B), .E5(B),
    .E6(B), .in_33(in_4), .out_34(out_6));  // open: E7, E8, E9, E10, E11, E12, E13, E14, E15, E16, E17, E18, E19, E20, E21, E22, E23, E24, E25, E26, E27, E28, E29, E30, E31
endmodule

module MUX8 (
  input  E0,
  input  E1,
  input  E2,
  input  E3,
  input  E4,
  input  E5,
  input  E6,
  input  E7,
  input  B,
  input  C,
  input  A,
  output out_12
);

  wire mux4_1_out_7, mux4_2_out_7;

  MUX4 mux4_1 (.in_1(E0), .in_2(E1), .in_3(E2), .in_4(E3), .in_5(C), .in_6(A), .out_7(mux4_1_out_7));
  MUX4 mux4_2 (.in_1(E4), .in_2(E5), .in_3(E6), .in_4(E7), .in_5(C), .in_6(A), .out_7(mux4_2_out_7));
  MUX2 mux2_1 (.E0(mux4_1_out_7), .E1(mux4_2_out_7), .E(B), .out_4(out_12));
endmodule

module ShiftLeftLogico (
  input  [31:0] in_1,
  input  in_2,
  output [31:0] out_3
);

  MUX2maisbits mux2maisbits_1 (.E0(in_1), .E1({in_1[30:0], 1'b0}), .E(in_2), .out_4(out_3));
endmodule

module MUX2maisbits (
  input  [31:0] E0,
  input  [31:0] E1,
  input  E,
  output [31:0] out_4
);

  wire [31:0] and_1_out, and_2_out;

  assign and_1_out = E0 & ~{32{E}};  // AND_Gate and_1, 32 bits wide
  assign and_2_out = E1 & {32{E}};  // AND_Gate and_2, 32 bits wide
  assign out_4 = and_1_out | and_2_out;  // OR_Gate or_1, 32 bits wide
endmodule

module ShiftRightLogico (
  input  [31:0] in_1,
  input  in_2,
  output [31:0] out_3
);

  MUX2maisbits mux2maisbits_1 (.E0(in_1), .E1({1'b0, in_1[31:1]}), .E(in_2), .out_4(out_3));
endmodule

module ShiftRightArit (
  input  [31:0] in_1,
  input  Shift,
  output [31:0] out_3
);

  MUX2maisbits mux2maisbits_1 (.E0(in_1), .E1({{2{in_1[31]}}, in_1[30:1]}), .E(Shift), .out_4(out_3));
endmodule

module ShiftLeftArit (
  input  [31:0] in_1,
  input  in_2,
  output [31:0] out_3
);

  MUX2maisbits mux2maisbits_1 (.E0(in_1), .E1({in_1[30:0], in_1[0]}), .E(in_2), .out_4(out_3));
endmodule
